# Fritzing sketch Smart Parking System (saved by Fritzing 0.9.2b)
breadboards: 1

parts:
  Part2 = Arduino Uno (Rev3)
  LED2 = LED - 5mm [color="Red (633nm)" package="5 mm [THT]"]  # not connected
  LCD1 = LCD screen
  R2 = Rotary Potentiometer (Large) [maximum_resistance=100kΩ package=THT]
  R3 = Resistor [tolerance=±5% resistance=220 package=THT]
  Part1 = SRF05 Ultrasonic Rangefinder
  Part3 = SRF05 Ultrasonic Rangefinder
  R4 = Photocell (LDR) [package=THT]
  R5 = Resistor [tolerance=±5% resistance=220 package="0402 [SMD]"]
  R6 = Photocell (LDR) [package=THT]
  R7 = Resistor [tolerance=±5% resistance=220 package="0402 [SMD]"]
  J1 = Basic Servo

nets:
  N1: Part2.A0, R4.pin_1, R5.Pin_0
  N2: Part2.A1, R6.pin_1, R7.Pin_0
  N3: Part2.D8, Part3.Echo
  N4: Part2.D9_PWM, Part3.Trig
  N5: Part2.D10_PWM/SS, Part1.Echo
  N6: Part2.D11_PWM/MOSI, J1.pulse
  N7: Part2.D13/SCK, Part1.Trig
  N8: Part2.D2, LCD1.RS
  N9: Part2.D3_PWM, LCD1.E
  N10: Part2.D4, LCD1.DB4
  N11: Part2.D5_PWM, LCD1.DB5
  N12: Part2.D6_PWM, LCD1.DB6
  N13: Part2.D7, LCD1.DB7
  VCC: Part2.5V, LCD1.VDD, R2.leg2, R3.Pin_0, Part1.VCC, Part3.VCC, R4.pin_0, R6.pin_0, J1.vcc
  GND: Part2.GND, LCD1.VSS, LCD1.R/W, LCD1.LED-, R2.leg1, Part1.GND, Part3.GND, R5.Pin_1, R7.Pin_1, J1.gnd
  N14: LCD1.V0, R2.wiper
  N15: LCD1.LED+, R3.Pin_1
